# Fritzing sketch Sketch 1(has buzzer,led and reverse) (saved by Fritzing 0.9.3b)
breadboards: 1

parts:
  Nano1 = Arduino Nano v2.3
  LED = smd LED [color="Red (633nm)" package="1206 [SMD]"]
  R1 = Resistor [tolerance=±5% resistance=220 package=THT]
  S1 = Pushbutton [package="[THT]"]
  SPKR1 = Loudspeaker
  R3 = Resistor [tolerance=±5% resistance=220 package=THT]
  Reverse = smd LED [color="Orange (612nm)" package="1206 [SMD]"]
  R2 = Resistor [tolerance=±5% resistance=220 package=THT]

nets:
  N1: Nano1.GND, LED.cathode, S1.Pin_1, S1.Pin_2, SPKR1.pin2, Reverse.cathode
  N2: Nano1.D10, R3.Pin_0
  N3: Nano1.D11, SPKR1.pin1
  N4: Nano1.D12, R2.Pin_0
  N5: Nano1.D13, R1.Pin_0
  N6: LED.anode, R2.Pin_1
  N7: R1.Pin_1, S1.Pin_3, S1.Pin_4
  N8: R3.Pin_1, Reverse.anode
